# Fritzing sketch BlueRCCar (saved by Fritzing 0.9.2b)
stripboards: 1

parts:
  U1 = attiny85 [package=dip]
  BT1 = Bluetooth HC-06u [package=THT]
  R1 = Resistor [tolerance=±5% resistance=10k package=THT]
  VCC_5V = Header 1 [package=1x01_offset]
  GND = Header 1 [package=1x01_offset]
  U2_VCC = Header 1 [package=1x01_offset]
  U2_GND = Header 1 [package=1x01_offset]
  U2_SDA = Header 1 [package=1x01_offset]
  U2_SCL = Header 1 [package=1x01_offset]
  R2 = Resistor [tolerance=±5% resistance=1k package=THT]
  R3 = Resistor [tolerance=±5% resistance=2.2k package=THT]
  U2_D0 = Header 1 [package=1x01_offset]
  U2_D1 = Header 1 [package=1x01_offset]
  U2_D2 = Header 1 [package=1x01_offset]
  U2_D3 = Header 1 [package=1x01_offset]
  U2_D4 = Header 1 [package=1x01_offset]
  U2_D5 = Header 1 [package=1x01_offset]
  U2_D6 = Header 1 [package=1x01_offset]
  U2_D7 = Header 1 [package=1x01_offset]  # not connected
  Q1 = Basic FET P-Channel [part_number=BS250 package="TO220 [THT]"]
  Q2 = Basic FET P-Channel [part_number=BS250 package="TO220 [THT]"]

nets:
  N1: U1.Pin_1, R1.Pin_0
  N2: U1.Pin_2, R2.Pin_1
  N3: U1.Pin_3, BT1.TXD
  N4: U1.Pin_4, BT1.GND, GND.1, U2_GND.1, R3.Pin_0
  N5: U1.Pin_5, U2_SDA.1
  N6: U1.Pin_7, U2_SCL.1
  N7: U1.Pin_8, BT1.VCC, R1.Pin_1, VCC_5V.1, U2_VCC.1, Q1.source, Q2.source
  N8: BT1.RXD, R2.Pin_0, R3.Pin_1
  N9: U2_D0.1, Q1.gate
  N10: U2_D1.1, Q2.gate
  Left: U2_D2.1
  Right: U2_D3.1
  Front Light: U2_D4.1
  Rear Light: U2_D5.1
  Horn: U2_D6.1
  Forward: Q1.drain
  Backward: Q2.drain

notes:
  PCF8574
  Breakout

custom parts:
  Bluetooth HC-06u: Bluetooth HC-06 - face up, pins down 16.5mm x 37.5mm PCB
